# Fritzing sketch Sketch (saved by Fritzing 1.0.2b)
# 18650 Li-ion Battery: CC-BY Dr Kristofer Chan, King's College London/Remote-research.org
circuit board: 8.46667cm x 5.64444cm
breadboards: 1

parts:
  U1 = attiny85 [package=dip]
  BAT1 = 18650 Li-ion Battery [package=battery-18650]
  BAT2 = 18650 Li-ion Battery [package=battery-18650]
  TP4056 = TP4056 [chip_label=TP4056 package="DIP (Dual Inline) [THT]"]
  Zonnepaneel_5V = Solar Cell
  part = Resistor [tolerance=±5% power=0.25W resistance=10k package=THT]
  part_2 = Resistor [tolerance=±5% power=0.25W resistance=10k package=THT]
  MT3608 = MT3608 Module
  U2 = WS2812 RGB LED matrix 1x8  # not connected
  IRLZ44N = Basic FET N-Channel [package="TO220 [THT]"]
  Mode_select = Pushbutton [package="[THT]"]
  part_3 = Resistor [tolerance=±5% power=0.25W resistance=330 package=THT]
  part_4 = Resistor [tolerance=±5% power=0.25W resistance=330 package=THT]
  part_5 = Resistor [tolerance=±5% power=0.25W resistance=10k package=THT]
  part_6 = Schottky Diode [part_number=1N5817 package="300 mil [THT]"]
  part_7 = Electrolytic Capacitor [capacitance=1000μF voltage=35V package="100 mil [THT, electrolytic]"]
  JP1 = Header 3 [package=screwterminal-3.5mm-3_lock.007s]
  JP2 = Header 2 [package=molex-1x2_lock]  # not connected

nets:
  N1: U1.Pin_2, part_4.Pin_1
  N2: U1.Pin_4, MT3608.pin4, IRLZ44N.source, Mode_select.Pin_3, Mode_select.Pin_4, part_5.Pin_1
  N3: U1.Pin_5, part_3.Pin_0
  N4: U1.Pin_6, Mode_select.Pin_1, Mode_select.Pin_2
  N5: U1.Pin_7, part.Pin_1, part_2.Pin_0
  N6: U1.Pin_8, MT3608.pin3, part_7.+, JP1.2
  N7: BAT1.-, BAT2.-, TP4056.pin5
  N8: BAT1.+, BAT2.+, TP4056.pin4
  N9: TP4056.pin1, part.Pin_0, part_6.cathode
  N10: TP4056.pin2, Zonnepaneel_5V.-, part_2.Pin_1
  N11: TP4056.pin3, MT3608.pin2
  N12: TP4056.pin6, MT3608.pin1
  N13: Zonnepaneel_5V.+, part_6.anode
  N14: IRLZ44N.gate, part_4.Pin_0, part_5.Pin_0
  N15: IRLZ44N.drain, part_7.-, JP1.1
  N16: part_3.Pin_1, JP1.3

custom parts:
  18650 Li-ion Battery: 18650 li-ion Battery Standard 18650 battery with interactive connectors Creative Common Attribution 4.0 International (CC-BY 4.0) license. Any use of this part requires attribution of Dr Kristofer Chan, Department of Geography, King's College London. Contact kristofer.chan [at] kcl.ac.uk OR kris [at] remote-research.org for further information.
  TP4056: A DIP stand-in part for whatever IC you want. With 6 pins on a 300mil dual inline package (DIP) footprint.
  MT3608 Module: MT3608 Boost Converter Module Links: Aerosemi MT3608 2A Step Up Converter datasheet
  WS2812 RGB LED matrix 1x8: WS2812 matrix 1x8
